// Logisim project MSF.circ as structural Verilog: 3 circuits, main circuit main
module main (
  input  X,
  output out_2
);

  wire clock_1_out, latchd_1_q, latchd_2_q, latchd_3_q, statoprossimo_1_b_prime_0, statoprossimo_1_b_prime_1,
       statoprossimo_1_b_prime_2;

  Clock clock_1 (.out(clock_1_out));
  Statoprossimo statoprossimo_1 (
    .X(X), .b0(latchd_1_q), .b1(latchd_2_q), .b2(latchd_3_q), .b_prime_0(statoprossimo_1_b_prime_0),
    .b_prime_1(statoprossimo_1_b_prime_1), .b_prime_2(statoprossimo_1_b_prime_2));
  latchD latchd_1 (.D(statoprossimo_1_b_prime_0), .in_2(clock_1_out), .Q(latchd_1_q));  // open: notQ
  latchD latchd_2 (.D(statoprossimo_1_b_prime_1), .in_2(clock_1_out), .Q(latchd_2_q));  // open: notQ
  latchD latchd_3 (.D(statoprossimo_1_b_prime_2), .in_2(clock_1_out), .Q(latchd_3_q));  // open: notQ
  \output  output_1 (.out_4(out_2), .b0(latchd_1_q), .b1(latchd_2_q), .b2(latchd_3_q));
endmodule

module \output  (
  input  b0,
  input  b1,
  input  b2,
  output out_4
);

  wire and_1_out, and_2_out;

  and and_1 (and_1_out, ~b0, b1, ~b2);  // AND_Gate
  and and_2 (and_2_out, b0, ~b1, b2);  // AND_Gate
  or or_1 (out_4, and_1_out, and_2_out);
endmodule

module Statoprossimo (
  input  X,
  input  b0,
  input  b1,
  input  b2,
  output b_prime_0,
  output b_prime_1,
  output b_prime_2
);


  assign b_prime_0 = X;
  assign b_prime_1 = b0;
  assign b_prime_2 = b1;
  // also tied to GND on the sheet: b2
endmodule
