// Logisim project NANDcircuit.circ as structural Verilog: 1 circuit, main circuit main
module main (
  input  A,
  input  B,
  input  C,
  output NAND,
  output TEST,
  output BASE
);

  wire nand_1_out, nand_2_out, nand_3_out, nand_4_out, nand_5_out, nand_6_out, nand_7_out, nand_8_out,
       nor_1_out, not_1_out, or_1_out;

  nand nand_1 (nand_1_out, A, A);
  nand nand_2 (nand_2_out, B, B);
  not not_1 (not_1_out, B);
  nor nor_1 (nor_1_out, A, B);
  or or_1 (or_1_out, C, not_1_out);
  nand nand_3 (nand_3_out, nand_1_out, nand_2_out);
  nand nand_4 (nand_4_out, nand_2_out, nand_2_out);
  nand nand_5 (nand_5_out, C, C);
  and and_1 (BASE, or_1_out, nor_1_out);
  nand nand_6 (nand_6_out, nand_3_out, nand_3_out);
  nand nand_7 (nand_7_out, nand_4_out, nand_5_out);
  nand nand_8 (nand_8_out, nand_6_out, nand_7_out);
  nand nand_9 (NAND, nand_8_out, nand_8_out);
  xnor xnor_1 (TEST, NAND, BASE);

  // Notes on the sheet:
  //   NOT B
endmodule
