// Logisim project SumDiff.circ as structural Verilog: 1 circuit, main circuit main
module main (
  input  [3:0] A,
  input  in_2,
  input  [3:0] B,
  output [3:0] out_4,
  output out_5,
  output out_6
);

  wire xor_5_out, xor_6_out;
  wire [3:0] xor_1_out;

  xor xor_1 (xor_1_out[0], in_2, B[0]);
  xor xor_2 (xor_1_out[1], in_2, B[1]);
  Adder #(.width(4)) adder_1 (.a(xor_1_out), .b(A), .out(out_4), .cin(in_2), .cout(out_5));
  xor xor_3 (xor_1_out[2], in_2, B[2]);
  xor xor_4 (xor_1_out[3], in_2, B[3]);
  xor xor_5 (xor_5_out, xor_1_out[3], out_4[3]);
  xor xor_6 (xor_6_out, out_4[3], A[3]);
  and and_1 (out_6, xor_5_out, xor_6_out);
endmodule
