// Logisim project bistabile.circ as structural Verilog: 8 circuits, main circuit main
module main (
  input  R,
  input  S,
  input  s_2,
  input  r_2,
  input  s_3,
  input  r_3,
  input  r_4,
  input  s_4,
  input  R_5,
  input  R_6,
  input  s_5,
  input  S_6,
  input  D,
  input  [3:0] in_14,
  input  w,
  input  [3:0] in_16,
  input  D_2,
  input  R_7,
  input  W_2,
  input  b_t,
  input  [3:0] in_21,
  input  R_8,
  input  w_3,
  input  S_7,
  input  b_t_2,
  input  [1:0] ADDRESS,
  input  [3:0] Word,
  output Q,
  output notQ,
  output out_30,
  output out_31,
  output out_32,
  output q_2,
  output notQ_2,
  output out_35,
  output Q_3,
  output Q_4,
  output notQ_3,
  output notQ_4,
  output Q_5,
  output notQ_5,
  output [3:0] out_42,
  output out_43,
  output [3:0] out_44,
  output [3:0] out_45,
  output [3:0] out_46,
  output [15:0] out_47
);

  wire and_1_out, and_2_out, and_3_out, and_4_out, and_5_out, and_7_out, and_8_out, and_11_out, and_12_out,
       and_13_out, and_14_out, and_15_out, and_16_out, and_17_out, and_18_out, and_19_out, and_20_out,
       clock_1_out, clock_2_out, clock_3_out, clock_4_out, clock_5_out, clock_6_out, clock_7_out,
       clock_8_out, clock_9_out, decoder_1_out0, decoder_1_out1, decoder_1_out2, decoder_1_out3, latchd_5_q,
       multiplexer_1_out, multiplexer_2_out, multiplexer_3_out, multiplexer_4_out, not_3_out, not_4_out,
       not_5_out, or_2_out, or_3_out, r_out, s_out;
  wire [3:0] and_9_out, and_10_out;
  wire [3:3] not_1_out, not_2_out;

  Clock clock_1 (.out(clock_1_out));
  and and_1 (and_1_out, clock_1_out, S_6);
  Clock clock_2 (.out(clock_2_out));
  Clock clock_3 (.out(clock_3_out));
  not not_1 (not_1_out[3], R_7);
  Clock clock_4 (.out(clock_4_out));
  not not_2 (not_2_out[3], R_8);
  Clock clock_5 (.out(clock_5_out));
  Decoder #(.select(2)) decoder_1 (
    .out0(decoder_1_out0), .out1(decoder_1_out1), .out2(decoder_1_out2), .out3(decoder_1_out3), .sel(ADDRESS));  // open: en
  nor nor_1 (Q, R, notQ);
  nor nor_2 (notQ, Q, S);
  and and_2 (and_2_out, ~s_2, ~r_2);  // AND_Gate
  and and_3 (and_3_out, s_2, ~r_2);  // AND_Gate
  and and_4 (and_4_out, ~s_3, ~r_3);  // AND_Gate
  and and_5 (and_5_out, s_3, ~r_3);  // AND_Gate
  or or_1 (out_32, out_35, s_4);
  and and_6 (out_35, out_32, ~r_4);  // AND_Gate
  and and_7 (and_7_out, R_5, clock_1_out);
  nor nor_3 (Q_3, and_7_out, notQ_3);
  nor nor_4 (notQ_3, Q_3, and_1_out);
  and and_8 (and_8_out, clock_2_out, w);
  assign and_9_out = in_16 & {4{not_1_out[3]}};  // AND_Gate and_9, 4 bits wide
  or or_2 (or_2_out, R_7, W_2);
  flip_flop flip_flop_1 (.D(b_t), .in_2(clock_4_out), .out_3(out_45[0]));
  assign and_10_out = in_21 & {4{not_2_out[3]}};  // AND_Gate and_10, 4 bits wide
  or or_3 (or_3_out, R_8, w_3, S_7);
  Clock clock_6 (.out(clock_6_out));
  and and_11 (and_11_out, out_30, and_2_out);
  and and_12 (and_12_out, out_31, and_4_out);
  and and_13 (and_13_out, 1'b1, and_5_out);
  latchD latchd_1 (.D(in_14[0]), .in_2(and_8_out), .Q(out_42[0]));  // open: notQ
  latchD latchd_2 (.D(in_14[1]), .in_2(and_8_out), .Q(out_42[1]));  // open: notQ
  latchD latchd_3 (.D(in_14[2]), .in_2(and_8_out), .Q(out_42[2]));  // open: notQ
  latchD latchd_4 (.D(in_14[3]), .in_2(and_8_out), .Q(out_42[3]));  // open: notQ
  flip_flop flip_flop_2 (.D(out_45[0]), .in_2(clock_4_out), .out_3(out_45[1]));
  and and_14 (and_14_out, clock_5_out, or_3_out);
  not not_3 (not_3_out, S_7);
  and and_15 (and_15_out, clock_6_out, decoder_1_out0);
  and and_16 (and_16_out, clock_6_out, decoder_1_out1);
  and and_17 (and_17_out, clock_6_out, decoder_1_out2);
  and and_18 (and_18_out, clock_6_out, decoder_1_out3);
  or or_4 (out_30, and_11_out, and_3_out);
  or or_5 (out_31, and_12_out, and_13_out);
  memoria4bit memoria4bit_1 (.in_1(and_9_out), .clock(clock_3_out), .w(or_2_out), .out_4(out_44));
  flip_flop flip_flop_3 (.D(out_45[1]), .in_2(clock_4_out), .out_3(out_45[2]));
  Multiplexer multiplexer_1 (.in0(b_t_2), .in1(and_10_out[3]), .out(multiplexer_1_out), .sel(not_3_out));  // open: en
  flip_flop flip_flop_4 (.D(multiplexer_1_out), .in_2(and_14_out), .out_3(out_46[3]));
  Clock clock_7 (.out(clock_7_out));
  Clock clock_8 (.out(clock_8_out));
  flip_flop flip_flop_5 (.D(out_45[2]), .in_2(clock_4_out), .out_3(out_45[3]));
  Multiplexer multiplexer_2 (
    .in0(out_46[3]), .in1(and_10_out[2]), .out(multiplexer_2_out), .sel(not_3_out));  // open: en
  flip_flop flip_flop_6 (.D(multiplexer_2_out), .in_2(and_14_out), .out_3(out_46[2]));
  _4LtachD u_4ltachd_1 (
    .in_2(Word), .out_3(out_47[0]), .out_4(out_47[1]), .out_5(out_47[2]), .out_6(out_47[3]), .in_1(and_15_out));
  _4LtachD u_4ltachd_2 (
    .in_2(Word), .out_3(out_47[4]), .out_4(out_47[5]), .out_5(out_47[6]), .out_6(out_47[7]), .in_1(and_16_out));
  _4LtachD u_4ltachd_3 (
    .in_2(Word), .out_3(out_47[8]), .out_4(out_47[9]), .out_5(out_47[10]), .out_6(out_47[11]),
    .in_1(and_17_out));
  _4LtachD u_4ltachd_4 (
    .in_2(Word), .out_3(out_47[12]), .out_4(out_47[13]), .out_5(out_47[14]), .out_6(out_47[15]),
    .in_1(and_18_out));
  Button u_r (.out(r_out));
  Button u_s (.out(s_out));
  and and_19 (and_19_out, R_6, clock_7_out);
  and and_20 (and_20_out, clock_7_out, s_5);
  not not_4 (not_4_out, D);
  Clock clock_9 (.out(clock_9_out));
  Multiplexer multiplexer_3 (
    .in0(out_46[2]), .in1(and_10_out[1]), .out(multiplexer_3_out), .sel(not_3_out));  // open: en
  flip_flop flip_flop_7 (.D(multiplexer_3_out), .in_2(and_14_out), .out_3(out_46[1]));
  nor nor_5 (q_2, r_out, notQ_2);
  nor nor_6 (notQ_2, q_2, s_out);
  latchASR latchasr_1 (.R(and_19_out), .S(and_20_out), .Q(Q_4), .notQ(notQ_4));
  latchSR latchsr_1 (.R(not_4_out), .clock(clock_8_out), .s(D), .Q(Q_5), .notQ(notQ_5));
  Multiplexer multiplexer_4 (
    .in0(out_46[1]), .in1(and_10_out[0]), .out(multiplexer_4_out), .sel(not_3_out));  // open: en
  flip_flop flip_flop_8 (.D(multiplexer_4_out), .in_2(and_14_out), .out_3(out_46[0]));
  latchD latchd_5 (.D(D_2), .in_2(clock_9_out), .Q(latchd_5_q));  // open: notQ
  not not_5 (not_5_out, clock_9_out);
  latchD latchd_6 (.D(latchd_5_q), .in_2(not_5_out), .Q(out_43));  // open: notQ

  // Other names for the same wires on the sheet: notQ_t = notQ_2; Q_t = q_2

  // Notes on the sheet:
  //   creare uno shfter a 4 bit
  //   AGGIUNGIAMO ORA UN CLOCK
  //   COSTRUIAMO UNA MEMORIA A 4 BIT
  //   Banco memoria di 4 bit con opzione di scrtittura RESET e shift
  //   COSTRUIRE UNA MEMORIA A 4 BIT CON OPZIONE DI RESET
  //   bistabile asincrono
  //   usiamo ora i tunnel e bottoni
  //   bistabile sincrono
  //   possiamo semplificare ancora
  //   retroazione per cui gli ingressi delle nostre porte logiche
  //   arrivano in momenti diversi
  //   aggiungere una porta in modo che la tt non cambi
  //   USIAMO IL CIRCUITO FATTO PRIMA
  //   prendo in input un valore di write in modo
  //   da andarea a scrivere solo quando c'e il segnale in input
  //   flip-flop usando fue latchD
endmodule

module latchASR (
  input  R,
  input  S,
  output Q,
  output notQ
);

  nor nor_1 (Q, R, notQ);
  nor nor_2 (notQ, Q, S);
endmodule

module latchSR (
  input  R,
  input  clock,
  input  s,
  output Q,
  output notQ
);

  wire and_1_out, and_2_out;

  and and_1 (and_1_out, R, clock);
  and and_2 (and_2_out, clock, s);
  latchASR latchasr_1 (.R(and_1_out), .S(and_2_out), .Q(Q), .notQ(notQ));
endmodule

module latchD (
  input  D,
  input  in_2,
  output Q,
  output notQ
);

  wire not_1_out;

  not not_1 (not_1_out, D);
  latchSR latchsr_1 (.R(not_1_out), .clock(in_2), .s(D), .Q(Q), .notQ(notQ));
endmodule

module memoria4bit (
  input  [3:0] in_1,
  input  clock,
  input  w,
  output [3:0] out_4
);

  wire and_1_out;

  and and_1 (and_1_out, clock, w);
  latchD latchd_1 (.D(in_1[0]), .in_2(and_1_out), .Q(out_4[0]));  // open: notQ
  latchD latchd_2 (.D(in_1[1]), .in_2(and_1_out), .Q(out_4[1]));  // open: notQ
  latchD latchd_3 (.D(in_1[2]), .in_2(and_1_out), .Q(out_4[2]));  // open: notQ
  latchD latchd_4 (.D(in_1[3]), .in_2(and_1_out), .Q(out_4[3]));  // open: notQ
endmodule

module flip_flop (
  input  D,
  input  in_2,
  output out_3
);

  wire latchd_1_q, not_1_out;

  latchD latchd_1 (.D(D), .in_2(in_2), .Q(latchd_1_q));  // open: notQ
  not not_1 (not_1_out, in_2);
  latchD latchd_2 (.D(latchd_1_q), .in_2(not_1_out), .Q(out_3));  // open: notQ
endmodule

module shifter (
  input  b_t,
  input  clock,
  output [3:0] out_3
);

  flip_flop flip_flop_1 (.D(b_t), .in_2(clock), .out_3(out_3[0]));
  flip_flop flip_flop_2 (.D(out_3[0]), .in_2(clock), .out_3(out_3[1]));
  flip_flop flip_flop_3 (.D(out_3[1]), .in_2(clock), .out_3(out_3[2]));
  flip_flop flip_flop_4 (.D(out_3[2]), .in_2(clock), .out_3(out_3[3]));
endmodule

module _4LtachD (
  input  in_1,
  input  [3:0] in_2,
  output out_3,
  output out_4,
  output out_5,
  output out_6
);

  latchD latchd_1 (.D(in_2[0]), .in_2(in_1), .Q(out_3));  // open: notQ
  latchD latchd_2 (.D(in_2[1]), .in_2(in_1), .Q(out_4));  // open: notQ
  latchD latchd_3 (.D(in_2[2]), .in_2(in_1), .Q(out_5));  // open: notQ
  latchD latchd_4 (.D(in_2[3]), .in_2(in_1), .Q(out_6));  // open: notQ
endmodule
