// Logisim project mult.circ as structural Verilog: 1 circuit, main circuit main
module main (
  input  [2:0] A,
  input  [2:0] B,
  output [5:0] out_3
);

  wire adder_1_cout, adder_2_cout, adder_2_out, adder_3_cout, adder_4_cout, and_2_out, and_3_out, and_4_out,
       and_5_out, and_6_out, and_7_out, and_8_out, and_9_out;

  and and_1 (out_3[0], A[0], B[0]);
  and and_2 (and_2_out, A[1], B[0]);
  and and_3 (and_3_out, B[0], A[2]);
  and and_4 (and_4_out, A[0], B[1]);
  and and_5 (and_5_out, A[1], B[1]);
  and and_6 (and_6_out, A[2], B[1]);
  and and_7 (and_7_out, A[0], B[2]);
  and and_8 (and_8_out, A[1], B[2]);
  and and_9 (and_9_out, A[1], B[2]);
  Adder #(.width(1)) adder_1 (.a(and_2_out), .b(and_4_out), .out(out_3[1]), .cout(adder_1_cout));  // open: cin
  Adder #(.width(1)) adder_2 (.a(and_3_out), .b(and_5_out), .out(adder_2_out), .cin(adder_1_cout), .cout(adder_2_cout));
  Adder #(.width(1)) adder_3 (.a(adder_2_out), .b(and_7_out), .out(out_3[2]), .cin(adder_2_cout), .cout(adder_3_cout));
  Adder #(.width(1)) adder_4 (.a(and_6_out), .b(and_8_out), .out(out_3[3]), .cin(adder_3_cout), .cout(adder_4_cout));
  Adder #(.width(1)) adder_5 (.a(adder_4_cout), .b(and_9_out), .out(out_3[4]), .cout(out_3[5]));  // open: cin
endmodule
