// Logisim project numeriPSEUDOCASUALI.circ as structural Verilog: 1 circuit, main circuit main
module main (
  input  write,
  input  [3:0] seed
);

  wire c, multiplexer_1_out, multiplexer_2_out, multiplexer_3_out, multiplexer_4_out, xor_1_out;
  wire [3:0] d_ff_1_q;

  Clock clock_1 (.out(c));
  LED led_1 (.in(xor_1_out));
  Multiplexer multiplexer_1 (.in0(xor_1_out), .in1(seed[0]), .out(multiplexer_1_out), .sel(write));  // open: en
  D_Flip_Flop d_ff_1 (.clk(c), .D(multiplexer_1_out), .Q(d_ff_1_q[0]));  // open: Qn, preset, en, reset
  Multiplexer multiplexer_2 (.in0(d_ff_1_q[0]), .in1(seed[1]), .out(multiplexer_2_out), .sel(write));  // open: en
  Hex_Digit_Display hex_digit_display_1 (.value(d_ff_1_q));  // open: dp
  D_Flip_Flop d_ff_2 (.clk(c), .D(multiplexer_2_out), .Q(d_ff_1_q[1]));  // open: Qn, preset, en, reset
  xor xor_1 (xor_1_out, d_ff_1_q[3], d_ff_1_q[2]);
  Multiplexer multiplexer_3 (.in0(d_ff_1_q[1]), .in1(seed[2]), .out(multiplexer_3_out), .sel(write));  // open: en
  D_Flip_Flop d_ff_3 (.clk(c), .D(multiplexer_3_out), .Q(d_ff_1_q[2]));  // open: Qn, preset, en, reset
  Multiplexer multiplexer_4 (.in0(d_ff_1_q[2]), .in1(seed[3]), .out(multiplexer_4_out), .sel(write));  // open: en
  D_Flip_Flop d_ff_4 (.clk(c), .D(multiplexer_4_out), .Q(d_ff_1_q[3]));  // open: Qn, preset, en, reset

  // Other names for the same wires on the sheet: s0 = seed[0]; s1 = seed[1]; s2 = seed[2]; s3 = seed[3]; w = write
endmodule
