// Logisim project orologio.circ as structural Verilog: 6 circuits, main circuit main
module main (
);

  wire clock_1_out, stop6_1_out_2, stop6_2_out_2, stop10_1_out_2, stop10_2_out_2;
  wire [3:0] counter4_1_out_3, counter4_2_out_3, counter4_3_out_3, counter4_4_out_3;

  Clock clock_1 (.out(clock_1_out));
  counter4 counter4_1 (.INPUT(clock_1_out), .CLEAR(stop10_1_out_2), .out_3(counter4_1_out_3));
  stop10 stop10_1 (.in_1(counter4_1_out_3), .out_2(stop10_1_out_2));
  counter4 counter4_2 (.INPUT(stop10_1_out_2), .CLEAR(stop6_1_out_2), .out_3(counter4_2_out_3));
  stop6 stop6_1 (.in_1(counter4_2_out_3), .out_2(stop6_1_out_2));
  counter4 counter4_3 (.INPUT(stop6_1_out_2), .CLEAR(stop10_2_out_2), .out_3(counter4_3_out_3));
  stop10 stop10_2 (.in_1(counter4_3_out_3), .out_2(stop10_2_out_2));
  counter4 counter4_4 (.INPUT(stop10_2_out_2), .CLEAR(stop6_2_out_2), .out_3(counter4_4_out_3));
  Hex_Digit_Display hex_digit_display_1 (.value(counter4_3_out_3));  // open: dp
  Hex_Digit_Display hex_digit_display_2 (.value(counter4_4_out_3));  // open: dp
  stop6 stop6_2 (.in_1(counter4_4_out_3), .out_2(stop6_2_out_2));
  Hex_Digit_Display hex_digit_display_3 (.value(counter4_2_out_3));  // open: dp
  Hex_Digit_Display hex_digit_display_4 (.value(counter4_1_out_3));  // open: dp
endmodule

module mod8 (
  input  [2:0] in_1,
  output [2:0] out_2
);

  wire and_1_out;

  not not_1 (out_2[0], in_1[0]);
  xor xor_1 (out_2[1], in_1[0], in_1[1]);
  and and_1 (and_1_out, in_1[0], in_1[1]);
  xor xor_2 (out_2[2], and_1_out, in_1[2]);
endmodule

module counter8 (
);

  wire clock_1_out;
  wire [2:0] d_ff_1_q, mod8_1_out_2;

  Clock clock_1 (.out(clock_1_out));
  D_Flip_Flop d_ff_1 (.clk(clock_1_out), .D(mod8_1_out_2[0]), .Q(d_ff_1_q[0]));  // open: Qn, preset, en, reset
  D_Flip_Flop d_ff_2 (.clk(clock_1_out), .D(mod8_1_out_2[1]), .Q(d_ff_1_q[1]));  // open: Qn, preset, en, reset
  D_Flip_Flop d_ff_3 (.clk(clock_1_out), .D(mod8_1_out_2[2]), .Q(d_ff_1_q[2]));  // open: Qn, preset, en, reset
  mod8 mod8_1 (.in_1(d_ff_1_q), .out_2(mod8_1_out_2));
  Hex_Digit_Display hex_digit_display_1 (.value({1'b0, d_ff_1_q}));  // open: dp
endmodule

module counter4 (
  input  INPUT,
  input  CLEAR,
  output [3:0] out_3
);

  wire j_k_ff_1_qn, j_k_ff_2_qn, j_k_ff_3_qn;

  J_K_Flip_Flop j_k_ff_1 (
    .J(1'b1), .clk(INPUT), .K(1'b1), .Q(out_3[0]), .Qn(j_k_ff_1_qn), .reset(CLEAR));  // open: preset, en
  J_K_Flip_Flop j_k_ff_2 (
    .J(1'b1), .clk(j_k_ff_1_qn), .K(1'b1), .Q(out_3[1]), .Qn(j_k_ff_2_qn), .reset(CLEAR));  // open: preset, en
  J_K_Flip_Flop j_k_ff_3 (
    .J(1'b1), .clk(j_k_ff_2_qn), .K(1'b1), .Q(out_3[2]), .Qn(j_k_ff_3_qn), .reset(CLEAR));  // open: preset, en
  J_K_Flip_Flop j_k_ff_4 (.J(1'b1), .clk(j_k_ff_3_qn), .K(1'b1), .Q(out_3[3]), .reset(CLEAR));  // open: Qn, preset, en
endmodule

module stop6 (
  input  [3:0] in_1,
  output out_2
);

  wire not_1_out, not_2_out;

  not not_1 (not_1_out, in_1[0]);
  not not_2 (not_2_out, in_1[3]);
  and and_1 (out_2, not_1_out, in_1[1], in_1[2], not_2_out);
endmodule

module stop10 (
  input  [3:0] in_1,
  output out_2
);

  wire not_1_out, not_2_out;

  not not_1 (not_1_out, in_1[0]);
  not not_2 (not_2_out, in_1[2]);
  and and_1 (out_2, not_1_out, in_1[1], not_2_out, in_1[3]);
endmodule
