// Logisim project sommaoreMSF.circ as structural Verilog: 3 circuits, main circuit main
module main (
  input  A,
  input  B,
  output out_3
);

  wire clock_1_out, latchd_1_q, latchd_2_q, tatoprossimo_1_r_prime, tatoprossimo_1_s_prime;

  Clock clock_1 (.out(clock_1_out));
  tatoprossimo tatoprossimo_1 (
    .A(A), .B(B), .R(latchd_2_q), .S_prime(tatoprossimo_1_s_prime), .R_prime(tatoprossimo_1_r_prime));  // open: S
  latchD latchd_1 (.D(tatoprossimo_1_s_prime), .in_2(clock_1_out), .Q(latchd_1_q));  // open: notQ
  latchD latchd_2 (.D(tatoprossimo_1_r_prime), .in_2(clock_1_out), .Q(latchd_2_q));  // open: notQ
  \output  output_1 (.S(latchd_1_q), .\output (out_3));
endmodule

module \output  (
  input  S,
  output \output 
);


  assign \output  = S;
endmodule

module tatoprossimo (
  input  A,
  input  B,
  input  S,
  input  R,
  output S_prime,
  output R_prime
);

  wire and_1_out, and_2_out, xor_1_out;

  xor xor_1 (xor_1_out, B, A);
  xor xor_2 (S_prime, R, xor_1_out);
  and and_1 (and_1_out, R, xor_1_out);
  and and_2 (and_2_out, B, A);
  or or_1 (R_prime, and_1_out, and_2_out);
  // also tied to GND on the sheet: S
endmodule
